# Fritzing sketch MainSCH (saved by Fritzing 1.0.3b)
breadboards: 1

parts:
  part = Arduino Uno (Rev3)
  Temperature_Sensor = TMP36 [package=to-92]
  R1 = Resistor [tolerance=±5% power=0.25W resistance=470 package=THT]
  SolarCell = S1133 Si Photodiode [package="8mm Ceramic [THT]"]
  WaterPump = DC Motor [voltage_(max)=6V voltage_(min)=3V]
  pumpSwithcTR = NPN-Transistor [package="TO92 [THT]"]
  WaterSRLeveler = Stepper Motor - Bipolar
  StepperMController = Pololu A4988 [package=SO16]
  Part2 = Soil Moisture Sensor
  LOWER = fc-51 [package=THT]
  UPPER = fc-51 [package=THT]
  S1 = Pushbutton [package=THT]

nets:
  N1: part.A1, SolarCell.cathode
  N2: part.D10_PWM/SS, StepperMController.STEP
  N3: part.D11_PWM/MOSI, StepperMController.DIR
  GND: part.GND, Temperature_Sensor.GND, SolarCell.anode, pumpSwithcTR.E, StepperMController.GND, Part2.GND, LOWER.pin2, UPPER.pin2, S1.leg1
  N4: part.D2, S1.leg0
  N5: part.D4, Temperature_Sensor.VOUT, R1.Pin_1
  12V: part.VIN, WaterPump.pin_1, StepperMController.VMOT
  5V: Temperature_Sensor.VCC, R1.Pin_0, StepperMController.VDD, LOWER.pin3, UPPER.pin3
  N6: WaterPump.pin_2, pumpSwithcTR.C
  A3 Arduino: pumpSwithcTR.B
  N7: WaterSRLeveler.A, StepperMController.2B
  N8: WaterSRLeveler.C, StepperMController.2A
  N9: WaterSRLeveler.B, StepperMController.1A
  N10: WaterSRLeveler.D, StepperMController.1B
  N11: StepperMController.RESET, StepperMController.SLEEP
  D7 - Arduino: Part2.VCC
  A0 - Arduino: Part2.SIG
  A5 - Arduino: LOWER.pin1
  A4 - Arduino: UPPER.pin1

notes:
  on TR: 1B, 2C, 3E
